# Fritzing sketch LegoCar_PCB_V1.0.0 (saved by Fritzing 0.9.3b)
circuit board: 6.5cm x 5.5cm
breadboards: 1

parts:
  SER = male pin header, 3 pins [form="♂ (male)"]
  GRB = male pin header, 4 pins [form="♂ (male)"]
  BAT = female pin header, 2 pins [form="♀ (female)"]
  ESC = male pin header, 3 pins [form="♂ (male)"]
  ESP = male pin header, 5 pins [form="♂ (male)"]
  MASTER = Arduino Nano (Rev3.0)
  SLAVE = Arduino Nano (Rev3.0)
  GPIO = female pin header, 3 pins [form="♀ (female)"]

nets:
  N1: SER.pin1, ESP.pin1, ESP.pin2, SLAVE.5V, GPIO.pin3
  N2: SER.pin2, MASTER.D11/MOSI
  GND: SER.pin3, BAT.pin1, ESC.pin3, ESP.pin3, MASTER.GND, SLAVE.GND, GPIO.pin1
  N3: GRB.pin1, SLAVE.D9
  N4: GRB.pin2, SLAVE.D10
  N5: GRB.pin3, SLAVE.D11/MOSI
  N6: GRB.pin4, SLAVE.D12/MISO
  VIN: BAT.pin2, MASTER.VIN, SLAVE.VIN
  N7: ESC.pin1, MASTER.D3
  N8: ESP.pin4, MASTER.D6
  N9: ESP.pin5, MASTER.D5
  N10: MASTER.D9, SLAVE.D6
  N11: MASTER.D10, SLAVE.D5
  N12: SLAVE.D3, GPIO.pin2

notes:
  +
  -
